# Fritzing sketch Electrical Scheme (saved by Fritzing 0.9.3b)
breadboards: 1

parts:
  Arduino = Arduino Uno (Rev3)
  VCC_+5V = 4 x AAA Battery Mount
  LED2_Forward = LED - 3mm [color="Blue (525nm)" package="3 mm [THT]"]
  LED1_Back = LED - 3mm [color="Red (660nm)" package="3 mm [THT]"]
  R3 = Resistor [tolerance=±5% resistance=220 package="0603 [SMD]"]
  R4 = Resistor [tolerance=±5% resistance=100 package="0603 [SMD]"]
  R2 = Resistor [tolerance=±5% resistance=10k package="0603 [SMD]"]
  R1 = Resistor [tolerance=±5% resistance=10k package="0603 [SMD]"]
  S2 = SWITCH-MOMENTARY-2 [package=tactile_switch_tall]
  S1 = SWITCH-MOMENTARY-2 [package=tactile_switch_tall]

nets:
  N1: Arduino.D8, R4.Pin_0
  N2: Arduino.GND, VCC_+5V.-, LED2_Forward.cathode, LED1_Back.cathode, S2.2, S1.2
  N3: Arduino.D2, R1.Pin_1, S1.1
  N4: Arduino.D3_PWM, R2.Pin_1, S2.1
  N5: Arduino.D7, R3.Pin_0
  N6: Arduino.VIN, R2.Pin_0, R1.Pin_0
  N7: LED2_Forward.anode, R3.Pin_1
  N8: LED1_Back.anode, R4.Pin_1
